# Fritzing sketch MinervaBoard 0.2 (saved by Fritzing 0.9.2b)
circuit board: 8.50345cm x 7.37698cm
breadboards: 1

parts:
  Power_plug1 = Power plug
  Fuse1 = Fuse with Handler [part_number=Htc-15m]
  Darlington_Driver_3 = ULN2803A [package=THT]
  Pad10 = Pad [width=2 height=1 connect=center]
  Pad11 = Pad [width=2 height=1 connect=center]
  Pad12 = Pad [width=2 height=1 connect=center]
  Pad13 = Pad [width=2 height=1 connect=center]
  Pad14 = Pad [width=2 height=1 connect=center]
  Pad15 = Pad [width=2 height=1 connect=center]
  Pad16 = Pad [width=2 height=1 connect=center]
  Pad17 = Pad [width=2 height=1 connect=center]
  Pin10 = Pad [width=2 height=1 connect=center]
  Pin11 = Pad [width=2 height=1 connect=center]
  Pin12 = Pad [width=2 height=1 connect=center]
  Pin13 = Pad [width=2 height=1 connect=center]
  Pin14 = Pad [width=2 height=1 connect=center]
  Pin15 = Pad [width=2 height=1 connect=center]
  Pin16 = Pad [width=2 height=1 connect=center]
  Pin17 = Pad [width=2 height=1 connect=center]
  Darlington_Driver_4 = ULN2803A [package=THT]
  Pad18 = Pad [width=2 height=1 connect=center]
  Pad19 = Pad [width=2 height=1 connect=center]
  Pad20 = Pad [width=2 height=1 connect=center]
  Pad21 = Pad [width=2 height=1 connect=center]
  Pad22 = Pad [width=2 height=1 connect=center]
  Pad23 = Pad [width=2 height=1 connect=center]
  Pad24 = Pad [width=2 height=1 connect=center]
  Pad25 = Pad [width=2 height=1 connect=center]
  Pin18 = Pad [width=2 height=1 connect=center]
  Pin19 = Pad [width=2 height=1 connect=center]
  Pin20 = Pad [width=2 height=1 connect=center]
  Pin21 = Pad [width=2 height=1 connect=center]
  Pin22 = Pad [width=2 height=1 connect=center]
  Pin23 = Pad [width=2 height=1 connect=center]
  Pin24 = Pad [width=2 height=1 connect=center]
  Pin25 = Pad [width=2 height=1 connect=center]
  Output_5 = IC, SIP package, 9 pins [chip_label=IC]
  R2 = Resistor [tolerance=±5% resistance=10k package="0603 [SMD]"]
  R3 = Resistor [tolerance=±5% resistance=10k package="0603 [SMD]"]
  R4 = Resistor [tolerance=±5% resistance=10k package="0603 [SMD]"]
  R5 = Resistor [tolerance=±5% resistance=10k package="0603 [SMD]"]
  R6 = Resistor [tolerance=±5% resistance=10k package="0603 [SMD]"]
  R7 = Resistor [tolerance=±5% resistance=10k package="0603 [SMD]"]
  R8 = Resistor [tolerance=±5% resistance=10k package="0603 [SMD]"]
  R9 = Resistor [tolerance=±5% resistance=10k package="0603 [SMD]"]
  R18 = Resistor [tolerance=±5% resistance=220 package="0603 [SMD]"]
  R19 = Resistor [tolerance=±5% resistance=220 package="0603 [SMD]"]
  Output_6 = IC, SIP package, 6 pins [chip_label=IC]
  ATMega = atmega328 [package=dip]
  R12 = Resistor [tolerance=±5% resistance=22k package="0603 [SMD]"]
  R16 = Resistor [tolerance=±5% resistance=22k package="0603 [SMD]"]
  R14 = Resistor [tolerance=±5% resistance=22k package="0603 [SMD]"]
  R10 = Resistor [tolerance=±5% resistance=22k package="0603 [SMD]"]
  R11 = Resistor [tolerance=±5% resistance=22k package="0603 [SMD]"]
  R1 = Resistor [tolerance=±5% resistance=22k package="0603 [SMD]"]
  R15 = Resistor [tolerance=±5% resistance=22k package="0603 [SMD]"]
  R13 = Resistor [tolerance=±5% resistance=22k package="0603 [SMD]"]
  Y1 = Resonator [frequency="16 MHz" package=THT]
  Level_Shifter = IC, DIP package, 20 pins [chip_label=IC]
  Pad27 = Pad [width=2 height=1 connect=center]
  Pad28 = Pad [width=2 height=1 connect=center]
  Pad29 = Pad [width=2 height=1 connect=center]
  Pad30 = Pad [width=2 height=1 connect=center]
  Pad31 = Pad [width=2 height=1 connect=center]
  Pad32 = Pad [width=2 height=1 connect=center]
  Pad33 = Pad [width=2 height=1 connect=center]
  Pad34 = Pad [width=2 height=1 connect=center]
  Pin27 = Pad [width=2 height=1 connect=center]
  Pin28 = Pad [width=2 height=1 connect=center]
  Pin29 = Pad [width=2 height=1 connect=center]
  Pin30 = Pad [width=2 height=1 connect=center]
  Pin31 = Pad [width=2 height=1 connect=center]
  Pin32 = Pad [width=2 height=1 connect=center]
  Pin33 = Pad [width=2 height=1 connect=center]
  Pin34 = Pad [width=2 height=1 connect=center]
  Output_8 = IC, SIP package, 9 pins [chip_label=IC]
  Pad35 = Pad [width=2 height=1 connect=center]
  Pin35 = Pad [width=2 height=1 connect=center]
  R21 = Resistor [tolerance=±5% resistance=220 package="0603 [SMD]"]
  Level_Shifter1 = IC, DIP package, 20 pins [chip_label=IC]
  Pad36 = Pad [width=2 height=1 connect=center]
  Pad37 = Pad [width=2 height=1 connect=center]
  Pad38 = Pad [width=2 height=1 connect=center]
  Pad39 = Pad [width=2 height=1 connect=center]
  Pad40 = Pad [width=2 height=1 connect=center]
  Pad41 = Pad [width=2 height=1 connect=center]
  Pad42 = Pad [width=2 height=1 connect=center]
  Pad43 = Pad [width=2 height=1 connect=center]
  Pad44 = Pad [width=2 height=1 connect=center]
  Pin36 = Pad [width=2 height=1 connect=center]
  Pin37 = Pad [width=2 height=1 connect=center]
  Pin38 = Pad [width=2 height=1 connect=center]
  Pin39 = Pad [width=2 height=1 connect=center]
  Pin40 = Pad [width=2 height=1 connect=center]
  Pin41 = Pad [width=2 height=1 connect=center]
  Pin42 = Pad [width=2 height=1 connect=center]
  Pin43 = Pad [width=2 height=1 connect=center]
  Pin44 = Pad [width=2 height=1 connect=center]
  Output_9 = IC, SIP package, 9 pins [chip_label=IC]
  R22 = Resistor [tolerance=±5% resistance=220 package="0603 [SMD]"]
  Output_4 = IC, SIP package, 10 pins [chip_label=IC]
  Output_7 = IC, SIP package, 9 pins [chip_label=IC]
  Output_3 = IC, SIP package, 10 pins [chip_label=IC]
  Raspberry_Pi1 = Raspberry Pi 2
  C2 = Ceramic Capacitor [capacitance=100nF package="0603 [SMD, multilayer]"]
  IC1 = SO08 [chip_label=IC package=SO]
  C1 = Ceramic Capacitor [capacitance=100nF package="0603 [SMD, multilayer]"]
  R20 = Resistor [tolerance=±5% resistance=10 package="0603 [SMD]"]
  R23 = Resistor [tolerance=±5% resistance=10k package="0603 [SMD]"]
  Output_10 = IC, SIP package, 4 pins [chip_label=IC]
  Output_11 = IC, SIP package, 7 pins [chip_label=IC]
  R24 = Resistor [tolerance=±5% resistance=100k package="0603 [SMD]"]
  R25 = Resistor [tolerance=±5% resistance=100k package="0603 [SMD]"]

nets:
  N1: Power_plug1.VCC, Fuse1.Connector1
  VCC: Fuse1.Connector2, Darlington_Driver_3.COM_-_Common, Darlington_Driver_4.COM_-_Common, Output_5.pin1, Output_6.pin3, ATMega.VCC, ATMega.AVCC, Pad35.pad, Output_4.pin2, Output_7.pin1, Output_3.pin2, Raspberry_Pi1.5V, IC1.7, R20.Pin_1, R23.Pin_1, Output_11.pin1, R25.Pin_0
  N2: Darlington_Driver_3.In_1, Pad14.pad, ATMega.D5_(PWM)
  N3: Darlington_Driver_3.In_2, Pad17.pad, ATMega.D4
  N4: Darlington_Driver_3.In_3, Pad12.pad, ATMega.D3_(PWM)
  N5: Darlington_Driver_3.In_4, Pad15.pad, ATMega.D2
  N6: Darlington_Driver_3.In_5, Pad11.pad, R19.Pin_0
  N7: Darlington_Driver_3.In_6, Pad10.pad, R18.Pin_0
  N8: Darlington_Driver_3.In_7, Pad13.pad, ATMega.A4, Output_7.pin7
  N9: Darlington_Driver_3.In_8, Pad16.pad, ATMega.A5, Output_7.pin8
  N10: Darlington_Driver_3.Out_8, Pin15.pad, Output_3.pin3
  N11: Darlington_Driver_3.Out_7, Pin12.pad, Output_3.pin4
  N12: Darlington_Driver_3.Out_6, Pin10.pad, Output_3.pin5
  N13: Darlington_Driver_3.Out_5, Pin14.pad, Output_3.pin6
  N14: Darlington_Driver_3.Out_4, Pin11.pad, Output_3.pin7
  N15: Darlington_Driver_3.Out_3, Pin13.pad, Output_3.pin8
  N16: Darlington_Driver_3.Out_2, Pin17.pad, Output_3.pin9
  N17: Darlington_Driver_3.Out_1, Pin16.pad, Output_3.pin10
  N18: Darlington_Driver_4.In_1, Pad22.pad, R2.Pin_0
  N19: Darlington_Driver_4.In_2, Pad25.pad, R3.Pin_0
  N20: Darlington_Driver_4.In_3, Pad20.pad, R4.Pin_0
  N21: Darlington_Driver_4.In_4, Pad23.pad, R5.Pin_0
  N22: Darlington_Driver_4.In_5, Pad19.pad, R6.Pin_0
  N23: Darlington_Driver_4.In_6, Pad18.pad, R7.Pin_0
  N24: Darlington_Driver_4.In_7, Pad21.pad, R8.Pin_0
  N25: Darlington_Driver_4.In_8, Pad24.pad, R9.Pin_0
  N26: Darlington_Driver_4.Out_8, Pin23.pad, Output_4.pin3
  N27: Darlington_Driver_4.Out_7, Pin20.pad, Output_4.pin4
  N28: Darlington_Driver_4.Out_6, Pin18.pad, Output_4.pin5
  N29: Darlington_Driver_4.Out_5, Pin22.pad, Output_4.pin6
  N30: Darlington_Driver_4.Out_4, Pin19.pad, Output_4.pin7
  N31: Darlington_Driver_4.Out_3, Pin21.pad, Output_4.pin8
  N32: Darlington_Driver_4.Out_2, Pin25.pad, Output_4.pin9
  N33: Darlington_Driver_4.Out_1, Pin24.pad, Output_4.pin10
  N34: Output_5.pin2, R9.Pin_1, ATMega.D6_(PWM), R16.Pin_1
  N35: Output_5.pin3, R8.Pin_1, ATMega.D7, R15.Pin_1
  N36: Output_5.pin4, R7.Pin_1, ATMega.D8, R14.Pin_1
  N37: Output_5.pin5, R6.Pin_1, ATMega.D9_(PWM), R12.Pin_1
  N38: Output_5.pin6, R5.Pin_1, ATMega.D10_(PWM), R13.Pin_1
  N39: Output_5.pin7, R4.Pin_1, ATMega.D11_(PWM), R11.Pin_1
  N40: Output_5.pin8, R3.Pin_1, ATMega.D12, R10.Pin_1
  N41: Output_5.pin9, R2.Pin_1, ATMega.D13, R1.Pin_1
  N42: R18.Pin_1, Output_6.pin4, ATMega.D0_(RX), IC1.8
  N43: R19.Pin_1, Output_6.pin5, ATMega.D1_(TX), IC1.5
  N44: Output_6.pin6, C1.1
  N45: ATMega.RESET, C1.0, R20.Pin_0
  N46: ATMega.XLAT1, Y1.0
  N47: ATMega.XLAT2, Y1.pin_1
  N48: ATMega.AREF, Output_7.pin2, C2.1
  N49: ATMega.A0, Output_7.pin3
  N50: ATMega.A1, Output_7.pin4
  N51: ATMega.A2, Output_7.pin5
  N52: ATMega.A3, Output_7.pin6
  N53: Level_Shifter.pin1, Raspberry_Pi1.GPIO23
  N54: Level_Shifter.pin2, Pad30.pad, Raspberry_Pi1.GPIO24
  N55: Level_Shifter.pin3, Pad27.pad, Raspberry_Pi1.GPIO25
  N56: Level_Shifter.pin4, Pad32.pad, Raspberry_Pi1.GPIO8
  N57: Level_Shifter.pin5, Pad29.pad, Raspberry_Pi1.GPIO7
  N58: Level_Shifter.pin6, Pad33.pad, Raspberry_Pi1.GPIO12
  N59: Level_Shifter.pin7, Pad34.pad, Raspberry_Pi1.GPIO16
  N60: Level_Shifter.pin8, Pad31.pad, Raspberry_Pi1.GPIO26
  N61: Level_Shifter.pin9, Pad28.pad, Raspberry_Pi1.GPIO20
  N62: Level_Shifter.pin11, Output_8.pin1, Pin35.pad, Pad37.pad
  N63: Level_Shifter.pin12, Pin29.pad, Output_8.pin2
  N64: Level_Shifter.pin13, Pin32.pad, Output_8.pin3
  N65: Level_Shifter.pin14, Pin34.pad, Output_8.pin4
  N66: Level_Shifter.pin15, Pin30.pad, Output_8.pin5
  N67: Level_Shifter.pin16, Pin33.pad, Output_8.pin6
  N68: Level_Shifter.pin17, Pin31.pad, Output_8.pin7
  N69: Level_Shifter.pin18, Pin27.pad, Output_8.pin8
  N70: Level_Shifter.pin19, Pin28.pad, Output_8.pin9, R21.Pin_0
  3V3: Level_Shifter.pin20, R21.Pin_1, Level_Shifter1.pin20, R22.Pin_1, Raspberry_Pi1.3v3, Raspberry_Pi1.3V3, IC1.3, Output_10.pin4
  N71: Level_Shifter1.pin1, Raspberry_Pi1.GPIO6
  N72: Level_Shifter1.pin2, Pad40.pad, Raspberry_Pi1.GPIO5
  N73: Level_Shifter1.pin3, Pad36.pad, Raspberry_Pi1.GPIO11
  N74: Level_Shifter1.pin4, Pad42.pad, Raspberry_Pi1.GPIO9
  N75: Level_Shifter1.pin5, Pad39.pad, Raspberry_Pi1.GPIO10
  N76: Level_Shifter1.pin6, Pad43.pad, Raspberry_Pi1.GPIO22
  N77: Level_Shifter1.pin7, Pad44.pad, Raspberry_Pi1.GPIO27
  N78: Level_Shifter1.pin8, Pad41.pad, Raspberry_Pi1.GPIO17
  N79: Level_Shifter1.pin9, Pad38.pad, Raspberry_Pi1.GPIO4
  N80: Level_Shifter1.pin11, Pin38.pad, Output_9.pin1
  N81: Level_Shifter1.pin12, Pin39.pad, Output_9.pin2
  N82: Level_Shifter1.pin13, Pin42.pad, Output_9.pin3
  N83: Level_Shifter1.pin14, Pin44.pad, Output_9.pin4
  N84: Level_Shifter1.pin15, Pin40.pad, Output_9.pin5
  N85: Level_Shifter1.pin16, Pin43.pad, Output_9.pin6
  N86: Level_Shifter1.pin17, Pin41.pad, Output_9.pin7
  N87: Level_Shifter1.pin18, Pin36.pad, Output_9.pin8
  N88: Level_Shifter1.pin19, Pin37.pad, Output_9.pin9, R22.Pin_0
  N89: Raspberry_Pi1.GPIO2, Output_10.pin3
  N90: Raspberry_Pi1.GPIO3, Output_10.pin2
  N91: Raspberry_Pi1.GPIO19, Output_11.pin7
  N92: Raspberry_Pi1.GPIO21, Output_11.pin5
  N93: Raspberry_Pi1.GPIO18, Output_11.pin6
  N94: Raspberry_Pi1.GPIO15, IC1.4
  N95: Raspberry_Pi1.GPIO14, IC1.1
  N96: IC1.6, R23.Pin_0
  N97: Output_11.pin4, R24.Pin_1, R25.Pin_1

notes:
  Short To Bypass Darlington
  5V
  Darlington Array (ULN2803A)
  Short Or 10k Rsist
  1k Rsist
  16MHz Oscillator
  Open Or 22k Pulldown Resistors
  Level Shifter (SN74LVC245A)
  Short for Darlington
  -> Darlington (ULN2803A) or
  ARef
  A0
  A1
  A2
  A3
  A4
  A5
  D6
  D7
  D8
  D9
  D10
  D11
  D12
  D13
  D6 - D13 Direct
  Darlington GPIO
  Level Shift GPIO
  Short for
  for Level
  10k Rsist
  D0
  D1
  D2
  D3
  D4
  D5
  Pi2
  Pi3
  Gnd
  Pi24
  Pi25
  Pi8
  Pi7
  Pi12
  Pi26
  Pi16
  3V
  Darlington
  DIR=Pi23
  Pi5
  Pi11
  Pi9
  Pi10
  0.1uF Cap
  10k Resist
  TXS0102
  Arduino DIP (ATMEGA328)
  DIR=Pi6
  Adafruit MAX98357
  Vin
  LRC
  Shifter
  Gnd or Vin
  Gain Configuration
  Pi20
  Pi22
  Pi27
  Pi17
  Pi4
